# Fritzing sketch main (saved by Fritzing 0.9.4)
breadboards: 1

parts:
  Part1 = Arduino Nano (Rev3.0)
  Part2 = BlueSMiRF Silver [part_number=10269]
  Part3 = InvenSense MPU6050
  U1 = POT [package=alps_pot]
  Part4 = Black Joystick KY-023
  Part5 = Black Joystick KY-023
  U2 = Voltage Regulator - 5V [package="DPak [SMD]"]  # not connected

nets:
  N1: Part1.D2, Part4.SW
  N2: Part1.D3, Part5.SW
  N3: Part1.D4, Part3.SDA
  N4: Part1.D5, Part3.SCL
  N5: Part1.D11/MOSI, Part2.TX_5V
  N6: Part1.D12/MISO, Part2.RX_5V
  GND: Part1.GND, Part2.GND, Part3.GND, U1.S, Part4.GND, Part5.GND
  VCC: Part1.5V, Part2.VCC, Part3.VCC, U1.E, Part4.+5V, Part5.+5V
  N7: Part1.A4, U1.A
  N8: Part1.A3, Part5.VRy
  N9: Part1.A2, Part5.VRx
  N10: Part1.A1, Part4.VRy
  N11: Part1.A0, Part4.VRx

custom parts:
  BlueSMiRF Silver: Description: The BlueSMiRF Silver is the latest Bluetooth wireless serial cable replacement from SparkFun Electronics! This version of the popular BlueSMiRF uses the RN-42 module which has a bit less range than the RN-41 module used in the BlueSMiRF Gold. These modems work as a serial (RX/TX) pipe. Any serial stream from 2400 to 115200bps can be passed seamlessly from your computer to your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
  Black Joystick KY-023: Description: The joystick is a combination of 2 analoog potentiometer and a digital switch. Arduino GND --> Module pin - Arduino +5V --> Module pin +5V Arduino Analoog 0 --> Module VRx Arduino Analoog 1 --> Module VRy Arduino Digital --> Module SW Dimensions: 1" x 1.25"
